# Fritzing sketch coin (saved by Fritzing 0.9.0b)
breadboards: 1

parts:
  Part1 = Arduino Uno (Rev3)
  J1 = ATX24 Pin Power Supply Connector [package=atx24_right_angle]
  R1 = Resistor [tolerance=±5% resistance=10k package=THT]
  Part2 = Coin Acceptor - 6-Coin version
  U1 = LCD-16X2 [package=lcd-16x2]  # not connected

nets:
  GND: Part1.GND, J1.GND, Part2.GND
  N1: Part1.D3_PWM, R1.Pin_1, Part2.SIG
  N2: Part1.5V, R1.Pin_0
  12V: J1.12V, Part2.12V

notes:
  I2C/SPI backpack
  SCL(A5) = Gray color
  SDA(A4) = Blue color

custom parts:
  Coin Acceptor - 6-Coin version: 12V coin acceptor that can handle up to 6 different denominations. Output is either pulse width, serial, or single pin per coin value.
